// Logisim project 1BitALU.circ as structural Verilog: 1 circuit, main circuit main
module main (
  input  A_inverter,
  input  B_inverter,
  input  A,
  input  B,
  input  C_in,
  input  [1:0] Operation,
  output RESULT,
  output C_out
);

  wire and_1_out, and_2_out, and_3_out, multiplexer_1_out, multiplexer_2_out, not_1_out, not_2_out, or_1_out,
       undriven, xor_1_out, xor_2_out;

  not not_1 (not_1_out, B);
  Multiplexer #(.enable("false")) multiplexer_1 (.in0(A), .in1(not_2_out), .out(multiplexer_1_out), .sel(A_inverter));
  not not_2 (not_2_out, A);
  Multiplexer #(.enable("false")) multiplexer_2 (.in0(B), .in1(not_1_out), .out(multiplexer_2_out), .sel(B_inverter));
  and and_1 (and_1_out, multiplexer_1_out, multiplexer_2_out);
  or or_1 (or_1_out, multiplexer_1_out, multiplexer_2_out);
  xor xor_1 (xor_1_out, multiplexer_1_out, multiplexer_2_out);
  and and_2 (and_2_out, xor_1_out, C_in);
  and and_3 (and_3_out, multiplexer_1_out, multiplexer_2_out);
  xor xor_2 (xor_2_out, xor_1_out, C_in);
  or or_2 (C_out, and_2_out, and_3_out);
  Multiplexer #(.enable("false"), .select(2)) multiplexer_3 (
    .in0(and_1_out), .in1(or_1_out), .in2(xor_2_out), .in3(undriven), .out(RESULT), .sel(Operation));

  // Notes on the sheet:
  //   Operation 00 => AND
  //   Operation 01 => OR
  //   Operation 10 => ADD
  //   1-bit ALU
  //   Full Adder
  //   Operation 11 => NO OP or NOT SUPPORTED
endmodule
