// Logisim project 1BitALU_DEMO.circ as structural Verilog: 4 circuits, main circuit AU
module AU (
  input  A,
  input  B,
  input  f,
  output S,
  output C
);

  wire and_1_out, and_2_out, xor_1_out;

  xor xor_1 (xor_1_out, A, B);
  and and_1 (and_1_out, xor_1_out, f);
  and and_2 (and_2_out, A, B);
  xor xor_2 (S, xor_1_out, f);
  or or_1 (C, and_1_out, and_2_out);

  // Notes on the sheet:
  //   Addition CarryIn 0 
  //   Subtraction CarryIn 1 
  //   1-bit Full Adder ALU
endmodule

module LU (
  input  A,
  input  B,
  input  f2,
  input  f0,
  output Result
);

  wire and_1_out, or_1_out, xor_1_out;

  and and_1 (and_1_out, A, B);
  or or_1 (or_1_out, A, B);
  xor xor_1 (xor_1_out, A, B);
  Multiplexer #(.enable("false"), .select(2)) multiplexer_1 (
    .in0(and_1_out), .in1(or_1_out), .in2(xor_1_out), .in3(B), .out(Result), .sel({f0, f2}));

  // Notes on the sheet:
  //   Logic Unit
endmodule

module ALU (
  input  A,
  input  B,
  input  [3:0] opcode,
  output Y,
  output C
);

  wire au_1_s, lu_1_result, multiplexer_1_out, multiplexer_2_out, not_1_out, not_2_out;

  Multiplexer #(.enable("false")) multiplexer_1 (.in0(A), .in1(not_1_out), .out(multiplexer_1_out), .sel(opcode[0]));
  not not_1 (not_1_out, A);
  Multiplexer #(.enable("false")) multiplexer_2 (.in0(B), .in1(not_2_out), .out(multiplexer_2_out), .sel(opcode[1]));
  not not_2 (not_2_out, B);
  AU au_1 (.A(multiplexer_1_out), .B(multiplexer_2_out), .f(opcode[2]), .S(au_1_s), .C(C));
  LU lu_1 (.A(A), .B(multiplexer_2_out), .f2(opcode[2]), .f0(opcode[0]), .Result(lu_1_result));
  Multiplexer #(.enable("false")) multiplexer_3 (.in0(au_1_s), .in1(lu_1_result), .out(Y), .sel(opcode[3]));

  // Notes on the sheet:
  //   Operation 01 => OR
  //   Operation 00 => AND
  //   Operation 10 => ADD
  //   Operation 11 => NO OP or NOT SUPPORTED
endmodule

module ALUtest (
  input  A,
  input  B,
  input  [3:0] opcode,
  output Result,
  output C,
  output Overflow
);

  ALU alu_1 (.A(A), .B(B), .opcode(opcode), .Y(Result), .C(C));
endmodule
