// Logisim project 1BitALU_latest.circ as structural Verilog: 7 circuits, main circuit ADD1
module ADD1 (
  input  A,
  input  B,
  input  f,
  output S,
  output C
);

  wire and_1_out, and_2_out, xor_1_out;

  xor xor_1 (xor_1_out, A, B);
  xor xor_2 (S, xor_1_out, f);
  and and_1 (and_1_out, xor_1_out, f);
  and and_2 (and_2_out, A, B);
  or or_1 (C, and_1_out, and_2_out);
endmodule

module ADD4 (
  input  f,
  input  [3:0] A,
  input  [3:0] B,
  output [3:0] S,
  output C
);

  wire add1_1_c, add1_2_c, add1_3_c;

  ADD1 add1_1 (.A(A[0]), .B(B[0]), .f(f), .S(S[0]), .C(add1_1_c));
  ADD1 add1_2 (.A(A[1]), .B(B[1]), .f(add1_1_c), .S(S[1]), .C(add1_2_c));
  ADD1 add1_3 (.A(A[2]), .B(B[2]), .f(add1_2_c), .S(S[2]), .C(add1_3_c));
  ADD1 add1_4 (.A(A[3]), .B(B[3]), .f(add1_3_c), .S(S[3]), .C(C));
endmodule

module ADD8 (
  input  f,
  input  [7:0] A,
  input  [7:0] B,
  output [7:0] S,
  output C
);

  wire add4_1_c;

  ADD4 add4_1 (.f(f), .A(A[3:0]), .B(B[3:0]), .S(S[3:0]), .C(add4_1_c));
  ADD4 add4_2 (.f(add4_1_c), .A(A[7:4]), .B(B[7:4]), .S(S[7:4]), .C(C));
endmodule

module LU1 (
  input  A,
  input  B,
  input  f2,
  input  f0,
  output LUR
);

  wire and_1_out, or_1_out, xor_1_out;

  and and_1 (and_1_out, A, B);
  or or_1 (or_1_out, A, B);
  xor xor_1 (xor_1_out, A, B);
  Multiplexer #(.enable("false"), .select(2)) multiplexer_1 (
    .in0(and_1_out), .in1(or_1_out), .in2(xor_1_out), .in3(B), .out(LUR), .sel({f2, f0}));

  // Notes on the sheet:
  //   Logit Unit
  //   AND 0 0
  //   OR 0 1
  //   XOR 1 0
  //   B 11
endmodule

module LU4 (
  input  f0,
  input  f2,
  input  [3:0] A,
  input  [3:0] B,
  output [3:0] C
);

  LU1 lu1_1 (.A(A[0]), .B(B[0]), .f2(f2), .f0(f0), .LUR(C[0]));
  LU1 lu1_2 (.A(A[1]), .B(B[1]), .f2(f2), .f0(f0), .LUR(C[1]));
  LU1 lu1_3 (.A(A[2]), .B(B[2]), .f2(f2), .f0(f0), .LUR(C[2]));
  LU1 lu1_4 (.A(A[3]), .B(B[3]), .f2(f2), .f0(f0), .LUR(C[3]));
endmodule

module ALU1 (
  input  f,
  input  A,
  input  B,
  input  f2,
  input  f0,
  input  opcode,
  output C,
  output R
);

  wire add1_1_s, lu1_1_lur;

  ADD1 add1_1 (.A(A), .B(B), .f(f), .S(add1_1_s), .C(C));
  LU1 lu1_1 (.A(A), .B(B), .f2(f2), .f0(f0), .LUR(lu1_1_lur));
  Multiplexer #(.enable("false")) multiplexer_1 (.in0(add1_1_s), .in1(lu1_1_lur), .out(R), .sel(opcode));

  // Notes on the sheet:
  //   AND 0 0
  //   XOR 1 0
  //   OR 0 1
  //   B 11
endmodule

module ALU4 (
  input  f,
  input  f2,
  input  f0,
  input  opcode,
  input  [3:0] A,
  input  [3:0] B,
  output [3:0] out_7,
  output out_8
);

  wire alu1_1_c, alu1_2_c, alu1_3_c;

  ALU1 alu1_1 (.f(f), .A(A[0]), .B(B[0]), .f2(f2), .f0(f0), .opcode(opcode), .C(alu1_1_c), .R(out_7[0]));
  ALU1 alu1_2 (.f(alu1_1_c), .A(A[1]), .B(B[1]), .f2(f2), .f0(f0), .opcode(opcode), .C(alu1_2_c), .R(out_7[1]));
  ALU1 alu1_3 (.f(alu1_2_c), .A(A[2]), .B(B[2]), .f2(f2), .f0(f0), .opcode(opcode), .C(alu1_3_c), .R(out_7[2]));
  ALU1 alu1_4 (.f(alu1_3_c), .A(A[3]), .B(B[3]), .f2(f2), .f0(f0), .opcode(opcode), .C(out_8), .R(out_7[3]));

  // Notes on the sheet:
  //   AND 0 0
  //   OR 0 1
  //   XOR 1 0
  //   B 11
endmodule
