// Logisim project CombinationalLogicC.circ as structural Verilog: 1 circuit, main circuit main
module main (
  input  A,
  input  B,
  output C
);

  wire and_1_out, and_2_out, and_3_out, nand_1_out, nor_1_out, not_1_out, not_2_out, not_3_out, or_2_out,
       undriven, undriven_2, undriven_3, undriven_4, undriven_5, undriven_6, undriven_7, undriven_8;

  not not_1 (not_1_out, A);
  and and_1 (and_1_out, not_1_out, B);
  and and_2 (and_2_out, A, B);
  or or_1 (C, and_1_out, and_2_out);
  nand nand_1 (nand_1_out, undriven_3, undriven_4);
  nor nor_1 (nor_1_out, undriven, undriven_2);
  and and_3 (and_3_out, undriven_5, undriven_6);
  or or_2 (or_2_out, undriven_7, undriven_8);
  not not_2 (not_2_out, and_3_out);
  not not_3 (not_3_out, or_2_out);
endmodule
