// Logisim project KMap_Two_Inputs.circ as structural Verilog: 1 circuit, main circuit main
module main (
  input  A,
  input  B,
  input  in_3,
  input  in_4,
  input  in_5,
  input  in_6,
  input  in_7,
  input  in_8,
  output out_9,
  output out_10,
  output out_11,
  output out_12
);

  wire and_1_out, and_2_out, not_1_out, not_2_out, not_5_out;

  not not_1 (not_1_out, A);
  not not_2 (not_2_out, B);
  not not_3 (out_10, in_4);
  not not_4 (out_11, in_5);
  not not_5 (not_5_out, in_7);
  and and_1 (and_1_out, not_1_out, not_2_out);
  and and_2 (and_2_out, A, B);
  or or_1 (out_12, not_5_out, in_8);
  or or_2 (out_9, and_1_out, and_2_out);
endmodule
