// Logisim project LogicalOR_AND.circ as structural Verilog: 1 circuit, main circuit main
module main (
  input  A,
  input  in_2,
  input  in_3,
  input  in_4,
  input  in_5,
  input  in_6,
  output out_7,
  output out_8,
  output out_9,
  output out_10,
  output out_11,
  output out_12,
  output out_13,
  output out_14,
  output out_15,
  output out_16,
  output out_17,
  output out_18
);

  wire and_5_out, not_1_out, not_2_out, not_3_out, not_4_out, not_5_out, or_6_out;

  not not_1 (not_1_out, in_4);
  or or_1 (out_7, 1'b0, A);
  and and_1 (out_8, 1'b0, A);
  or or_2 (out_9, 1'b1, in_2);
  and and_2 (out_10, 1'b1, in_2);
  or or_3 (out_11, in_3, in_3);
  and and_3 (out_12, in_3, in_3);
  or or_4 (out_13, not_1_out, in_4);
  and and_4 (out_14, not_1_out, in_4);
  and and_5 (and_5_out, in_5, in_6);
  not not_2 (not_2_out, in_5);
  or or_5 (out_16, not_2_out, not_3_out);
  not not_3 (not_3_out, in_6);
  or or_6 (or_6_out, in_5, in_6);
  not not_4 (not_4_out, in_5);
  and and_6 (out_18, not_4_out, not_5_out);
  not not_5 (not_5_out, in_6);
  not not_6 (out_15, and_5_out);
  not not_7 (out_17, or_6_out);
endmodule
