// Logisim project intro_logic_block.circ as structural Verilog: 1 circuit, main circuit main
module main (
  input  in_1,
  input  in_2,
  input  in_3,
  input  in_4,
  input  in_5,
  input  in_6,
  input  in_7,
  input  in_8,
  input  in_9,
  input  in_10,
  input  in_11,
  output out_12,
  output out_13,
  output out_14,
  output out_15,
  output out_16,
  output out_17
);

  wire and_1_out, and_4_out, not_2_out, or_1_out;

  and and_1 (and_1_out, in_10, in_11);
  or or_1 (or_1_out, in_11, in_10);
  and and_2 (out_12, in_1, in_2);
  or or_2 (out_14, in_4, in_6);
  not not_1 (out_15, in_8);
  not not_2 (not_2_out, and_1_out);
  and and_3 (out_17, not_2_out, or_1_out);
  nand nand_1 (out_13, in_3, in_5);
  and and_4 (and_4_out, in_7, in_9);
  not not_3 (out_16, and_4_out);
endmodule
