// Logisim project myadder.circ as structural Verilog
module main (
  input  A,
  input  B,
  input  CARRY_IN,
  output CARRY_OUT,
  output SUM
);

  wire and_1_out, and_2_out, and_3_out, and_4_out, and_5_out, not_1_out, not_2_out, or_1_out;

  not not_1 (not_1_out, A);
  not not_2 (not_2_out, B);
  and and_1 (and_1_out, A, B);
  and and_2 (and_2_out, A, CARRY_IN);
  and and_3 (and_3_out, B, CARRY_IN);
  and and_4 (and_4_out, not_1_out, B);
  and and_5 (and_5_out, A, not_2_out);
  or or_1 (or_1_out, and_1_out, and_2_out);
  or or_2 (SUM, and_4_out, and_5_out);
  or or_3 (CARRY_OUT, or_1_out, and_3_out);

  // Notes on the sheet:
  //   Full Adder
  //   CarryOut Circuit
  //   Half Adder
endmodule
